// Logisim project ALU_181_base.circ as structural Verilog: 12 circuits, main circuit Processor
module Processor (
  input  Clk,
  input  [7:0] DataIn,
  input  Rst,
  input  Interrupt,
  input  [15:0] halt,
  input  run,
  input  single,
  output [7:0] debug_a,
  output [15:0] debug_bc,
  output [15:0] debug_de,
  output [15:0] debug_hl,
  output [15:0] debug_sp,
  output [15:0] Address,
  output [7:0] DataOut,
  output RnW,
  output last
);

  wire ALU_carry, ALU_sign, ALU_zero, and_1_out, C_flag, Clk_t, cmc, comparator_1_eq, d_ff_1_qn, Irq,
       not_1_out, not_2_out, or_1_out, S_flag, sequencer_1_inhibit_inc, stc, SysRST, WriteC, WriteZF, xchg,
       Z_flag;
  wire [1:0] sequencer_1_sel_add;
  wire [3:0] sequencer_1_alu_op, sequencer_1_dest, sequencer_1_src;
  wire [7:0] alu_1_result, Instruction, registers_1_accumulator, registers_1_register_out, sequencer_1_cycle;

  and and_1 (and_1_out, not_2_out, or_1_out);
  D_Flip_Flop d_ff_1 (.D(1'b1), .clk(not_1_out), .Qn(d_ff_1_qn), .reset(single));  // open: Q, preset
  not not_1 (not_1_out, last);
  and and_2 (Clk_t, Clk, and_1_out);
  not not_2 (not_2_out, comparator_1_eq);
  Comparator #(.width(16)) comparator_1 (.a(Address), .b(halt), .eq(comparator_1_eq));  // open: gt, lt
  or or_1 (or_1_out, run, d_ff_1_qn);
  LED led_1 (.in(Z_flag));
  LED led_2 (.in(C_flag));
  LED led_3 (.in(S_flag));
  // Probe on alu_1_result
  // Probe on Instruction
  Registers registers_1 (
    .Register_in(alu_1_result), .Din(DataIn), .CLK(Clk_t), .Destination(sequencer_1_dest),
    .Source(sequencer_1_src), .Address_sel(sequencer_1_sel_add), .Carry_in(ALU_carry), .Sign_in(ALU_sign),
    .Zero_in(ALU_zero), .Write_carry(WriteC), .Write_ZS(WriteZF), .Rst(SysRST), .Int(Irq), .Stc(stc),
    .Cmc(cmc), .Flip(xchg), .a(debug_a), .bc(debug_bc), .de(debug_de), .hl(debug_hl), .sp(debug_sp),
    .Accumulator(registers_1_accumulator), .Register_out(registers_1_register_out),
    .Instruction(Instruction), .Address_Bus(Address), .C_flag(C_flag), .Z_flag(Z_flag), .S_flag(S_flag),
    .Dout(DataOut), .ReadNotWrite(RnW));
  Sequencer sequencer_1 (
    .Instruction(Instruction), .CLK(Clk_t), .Reset(Rst), .irq(Interrupt), .VZero(Z_flag), .VCarry(C_flag),
    .VSign(S_flag), .Src(sequencer_1_src), .Dest(sequencer_1_dest), .Sel_Add(sequencer_1_sel_add),
    .ALU_Op(sequencer_1_alu_op), .Cf(WriteC), .Zsf(WriteZF), .Stc(stc), .Cmc(cmc), .Xchg(xchg), .Last(last),
    .Cycle(sequencer_1_cycle), .SysRST(SysRST), .SysINT(Irq), .Inhibit_Inc(sequencer_1_inhibit_inc));  // open: trig, stored
  // Probe on sequencer_1_src
  // Probe on sequencer_1_dest
  // Probe on sequencer_1_sel_add
  // Probe on sequencer_1_cycle
  // Probe on sequencer_1_alu_op
  // Probe on registers_1_register_out
  ALU alu_1 (
    .Input_A(registers_1_accumulator), .Input_B(registers_1_register_out), .Sel(sequencer_1_alu_op),
    .Carry_in(C_flag), .Clk(Clk_t), .Int(sequencer_1_inhibit_inc), .Result(alu_1_result),
    .Carry_out(ALU_carry), .Zero(ALU_zero), .Sign(ALU_sign));

  // Other names for the same wires on the sheet: ad[15:0] = Address; Din[7:0] = DataIn
endmodule

module Registers (
  input  [7:0] Register_in,
  input  [7:0] Din,
  input  CLK,
  input  [3:0] Destination,
  input  [3:0] Source,
  input  [1:0] Address_sel,
  input  Carry_in,
  input  Sign_in,
  input  Zero_in,
  input  Write_carry,
  input  Write_ZS,
  input  Rst,
  input  Int,
  input  Stc,
  input  Cmc,
  input  Flip,
  output [7:0] a,
  output [15:0] bc,
  output [15:0] de,
  output [15:0] hl,
  output [15:0] sp,
  output [7:0] Accumulator,
  output [7:0] Register_out,
  output [7:0] Instruction,
  output [15:0] Address_Bus,
  output C_flag,
  output Z_flag,
  output S_flag,
  output [7:0] Dout,
  output ReadNotWrite
);

  wire and_2_out, comparator_1_eq, decoder_1_out0, decoder_1_out1, decoder_1_out2, decoder_1_out3,
       decoder_1_out4, decoder_1_out5, decoder_1_out7, decoder_1_out8, decoder_1_out9, decoder_1_out10,
       decoder_1_out11, decoder_1_out12, decoder_1_out13, decoder_1_out15, flip_t, not_1_out, or_1_out;
  wire [3:0] dest, xchg_2_res;
  wire [7:0] and_1_out, flags_1_out_bus, H_q, L_q, MARH_q, MARL_q, multiplexer_4_out, multiplexer_5_out,
       PCH_q, PCL_q;
  wire [15:0] E_q, multiplexer_3_out;

  Decoder #(.select(4)) decoder_1 (
    .out0(decoder_1_out0), .out1(decoder_1_out1), .out2(decoder_1_out2), .out3(decoder_1_out3),
    .out4(decoder_1_out4), .out5(decoder_1_out5), .out7(decoder_1_out7), .out8(decoder_1_out8),
    .out9(decoder_1_out9), .out10(decoder_1_out10), .out11(decoder_1_out11), .out12(decoder_1_out12),
    .out13(decoder_1_out13), .out15(decoder_1_out15), .sel(dest), .en(CLK));  // open: out6, out14
  xchg xchg_1 (.flip(flip_t), .dest(Destination), .res(dest));
  J_K_Flip_Flop j_k_ff_1 (.J(Flip), .K(Flip), .clk(CLK), .Q(flip_t));  // open: Qn, preset, reset
  Register B (.D(Register_in), .clk(decoder_1_out0), .Q(bc[15:8]));  // open: en, clr
  Register H (.D(Register_in), .clk(decoder_1_out4), .Q(H_q));  // open: en, clr
  Register PCH (.D(Register_in), .clk(decoder_1_out8), .Q(PCH_q));  // open: en, clr
  Register MARH (.D(Register_in), .clk(decoder_1_out12), .Q(MARH_q));  // open: en, clr
  Register C (.D(Register_in), .clk(decoder_1_out1), .Q(bc[7:0]));  // open: en, clr
  Register L (.D(Register_in), .clk(decoder_1_out5), .Q(L_q));  // open: en, clr
  Register PCL (.D(Register_in), .clk(decoder_1_out9), .Q(PCL_q));  // open: en, clr
  Register MARL (.D(Register_in), .clk(decoder_1_out13), .Q(MARL_q));  // open: en, clr
  Flags flags_1 (
    .Carry_In(Carry_in), .In_Bus(Register_in), .Sign_In(Sign_in), .Zero_In(Zero_in), .Clock(CLK),
    .Dest(dest), .Write_Carry(Write_carry), .Write_ZS(Write_ZS), .Stc(Stc), .Cmc(Cmc),
    .Out_Bus(flags_1_out_bus), .C_Flag(C_flag), .Z_Flag(Z_flag), .S_Flag(S_flag));
  Multiplexer #(.width(16)) multiplexer_1 (.in0(E_q), .in1({H_q, L_q}), .out(de));  // open: sel
  Register D (.D(Register_in), .clk(decoder_1_out2), .Q(E_q[15:8]));  // open: en, clr
  Register SPH (.D(Register_in), .clk(decoder_1_out10), .Q(sp[15:8]));  // open: en, clr
  Multiplexer #(.width(16)) multiplexer_2 (.in0({H_q, L_q}), .in1(E_q), .out(hl));  // open: sel
  Multiplexer #(.width(16)) multiplexer_3 (.in0({H_q, L_q}), .in1(E_q), .out(multiplexer_3_out), .sel(flip_t));
  Multiplexer #(.width(8)) multiplexer_4 (.in0(8'hc7), .in1(8'hcf), .out(multiplexer_4_out), .sel(Int));
  Register E (.D(Register_in), .clk(decoder_1_out3), .Q(E_q[7:0]));  // open: en, clr
  Register Acc (.D(Register_in), .clk(decoder_1_out7), .Q(a));  // open: en, clr
  Register SPL (.D(Register_in), .clk(decoder_1_out11), .Q(sp[7:0]));  // open: en, clr
  Register IR (.D(multiplexer_5_out), .clk(decoder_1_out15), .Q(Instruction));  // open: en, clr
  Multiplexer #(.width(8)) multiplexer_5 (
    .in0(Register_in), .in1(multiplexer_4_out), .out(multiplexer_5_out), .sel(or_1_out));
  or or_1 (or_1_out, Int, Rst);
  Comparator #(.width(4)) comparator_1 (.a(dest), .b(4'b0110), .eq(comparator_1_eq));  // open: gt, lt
  Multiplexer #(.select(2), .width(16)) multiplexer_6 (
    .in0(multiplexer_3_out), .in1({PCH_q, PCL_q}), .in2(sp), .in3({MARH_q, MARL_q}), .out(Address_Bus),
    .sel(Address_sel));
  not not_1 (not_1_out, CLK);
  assign and_1_out = 8'h38 & Instruction;  // AND_Gate and_1, 8 bits wide
  and and_2 (and_2_out, comparator_1_eq, not_1_out);
  Multiplexer #(.select(4), .width(8)) multiplexer_7 (
    .in0(bc[15:8]), .in1(bc[7:0]), .in2(E_q[15:8]), .in3(E_q[7:0]), .in4(H_q), .in5(L_q), .in6(Din), .in7(a),
    .in8(PCH_q), .in9(PCL_q), .in10(sp[15:8]), .in11(sp[7:0]), .in12(MARH_q), .in13(MARL_q),
    .in14(flags_1_out_bus), .in15(and_1_out), .out(Register_out), .sel(xchg_2_res));
  assign Dout = and_2_out ? Register_in : 8'bz;  // Controlled_Buffer controlled_buffer_1
  not not_2 (ReadNotWrite, and_2_out);
  xchg xchg_2 (.flip(flip_t), .dest(Source), .res(xchg_2_res));

  assign Accumulator = a;

  // Other names for the same wires on the sheet: Mout[7:0] = Register_in

  // Notes on the sheet:
  //   Note: has to be valid when clock is low to enable data to the memory bus
endmodule

module ALU (
  input  [7:0] Input_A,
  input  [7:0] Input_B,
  input  [3:0] Sel,
  input  Carry_in,
  input  Clk,
  input  Int,
  output [7:0] Result,
  output Carry_out,
  output Zero,
  output Sign
);

  wire alu_internal_1_c, alu_internal_1_c_flipped, alu_internal_1_m, alu_internal_1_rar, alu_internal_1_rrc,
       B2A, hc181_1_c4, hc181_2_c4, internal_c_q, not_1_out;
  wire [3:0] alu_internal_1_command, hc181_1_f, hc181_2_f;
  wire [7:0] multiplexer_1_out;

  Hex_Digit_Display hex_digit_display_1 (.value(Input_A[7:4]));  // open: dp
  Hex_Digit_Display hex_digit_display_2 (.value(Input_B[7:4]));  // open: dp
  Hex_Digit_Display hex_digit_display_3 (.value(Input_B[3:0]));  // open: dp
  Hex_Digit_Display hex_digit_display_4 (.value(Input_A[3:0]));  // open: dp
  Multiplexer #(.width(8)) multiplexer_1 (.in0(Input_A), .in1(Input_B), .out(multiplexer_1_out), .sel(B2A));
  // Probe on alu_internal_1_command
  hc181 hc181_1 (
    .S(alu_internal_1_command), .A(multiplexer_1_out[3:0]), .B(Input_B[3:0]), .M(alu_internal_1_m),
    .Cin(alu_internal_1_c), .F(hc181_1_f), .C4(hc181_1_c4));  // open: G, P, AeqB
  hc181 hc181_2 (
    .S(alu_internal_1_command), .A(multiplexer_1_out[7:4]), .B(Input_B[7:4]), .M(alu_internal_1_m),
    .Cin(hc181_1_c4), .F(hc181_2_f), .C4(hc181_2_c4));  // open: G, P, AeqB
  ALU_internal alu_internal_1 (
    .Sel(Sel), .Cext(Carry_in), .Cint(internal_c_q), .Int(Int), .Command(alu_internal_1_command),
    .m(alu_internal_1_m), .c(alu_internal_1_c), .b2a(B2A), .rar(alu_internal_1_rar),
    .rrc(alu_internal_1_rrc), .c_flipped(alu_internal_1_c_flipped));
  Hex_Digit_Display hex_digit_display_5 (.value(hc181_2_f));  // open: dp
  Hex_Digit_Display hex_digit_display_6 (.value(hc181_1_f));  // open: dp
  not not_1 (not_1_out, hc181_2_c4);
  D_Flip_Flop internal_c (.D(hc181_2_c4), .clk(Clk), .Q(internal_c_q));  // open: Qn, preset, reset
  Hex_Digit_Display hex_digit_display_7 (.value(Result[7:4]));  // open: dp
  Rotate rotate_1 (
    .Input_ALU({hc181_2_f, hc181_1_f}), .Input_acc(Input_A), .Stored_carry(Carry_in), .Live_carry(not_1_out),
    .Rar(alu_internal_1_rar), .Rrc(alu_internal_1_rrc), .flip_c(alu_internal_1_c_flipped), .Result(Result),
    .Carry_out(Carry_out));
  Hex_Digit_Display hex_digit_display_8 (.value(Result[3:0]));  // open: dp
  nor nor_1 (Zero, Result[0], Result[1], Result[2], Result[3], Result[4], Result[5], Result[6], Result[7]);

  assign Sign = Result[7];

  // Other names for the same wires on the sheet: Acc[7:0] = Input_A; cy = Carry_in

  // Notes on the sheet:
  //   0: ADD
  //   1: ADC
  //   2: SUB
  //   3: SBB
  //   4: ANA
  //   5: XRA
  //   6: ORA
  //   7: CMP
  //   8: INCL
  //   9: INCH
  //   a: DECL
  //   b: DECH
  //   c: RAR
  //   d: RRC
  //   e: ZERO
  //   f: PASS
endmodule

module Flags (
  input  Carry_In,
  input  [7:0] In_Bus,
  input  Sign_In,
  input  Zero_In,
  input  Clock,
  input  [3:0] Dest,
  input  Write_Carry,
  input  Write_ZS,
  input  Stc,
  input  Cmc,
  output [7:0] Out_Bus,
  output C_Flag,
  output Z_Flag,
  output S_Flag
);

  wire and_1_out, and_2_out, Carry_qn, comparator_1_eq, multiplexer_1_out, multiplexer_2_out,
       multiplexer_3_out, multiplexer_4_out, multiplexer_5_out, or_1_out, or_2_out;

  Comparator #(.width(4)) comparator_1 (.a(Dest), .b(4'b1110), .eq(comparator_1_eq));  // open: gt, lt
  Multiplexer multiplexer_1 (.in0(Carry_In), .in1(In_Bus[0]), .out(multiplexer_1_out), .sel(comparator_1_eq));
  Multiplexer multiplexer_2 (.in0(Sign_In), .in1(In_Bus[7]), .out(multiplexer_2_out), .sel(comparator_1_eq));
  Multiplexer multiplexer_3 (.in0(Zero_In), .in1(In_Bus[6]), .out(multiplexer_3_out), .sel(comparator_1_eq));
  or or_1 (or_1_out, comparator_1_eq, Write_ZS);
  and and_1 (and_1_out, Clock, or_2_out);
  and and_2 (and_2_out, Clock, or_1_out);
  or or_2 (or_2_out, comparator_1_eq, Write_Carry);
  Multiplexer multiplexer_4 (.in0(multiplexer_1_out), .in1(1'b1), .out(multiplexer_4_out), .sel(Stc));
  Multiplexer multiplexer_5 (.in0(multiplexer_4_out), .in1(Carry_qn), .out(multiplexer_5_out), .sel(Cmc));
  D_Flip_Flop Carry (.D(multiplexer_5_out), .clk(and_1_out), .Q(C_Flag), .Qn(Carry_qn));  // open: preset, reset
  D_Flip_Flop Zero (.D(multiplexer_3_out), .clk(and_2_out), .Q(Out_Bus[6]));  // open: Qn, preset, reset
  D_Flip_Flop Sign (.D(multiplexer_2_out), .clk(and_2_out), .Q(Out_Bus[7]));  // open: Qn, preset, reset

  assign Out_Bus[5:0] = {{5{1'b0}}, C_Flag};
  assign S_Flag = Out_Bus[7];
  assign Z_Flag = Out_Bus[6];
endmodule

module Sequencer (
  input  [7:0] Instruction,
  input  CLK,
  input  Reset,
  input  irq,
  input  VZero,
  input  VCarry,
  input  VSign,
  output [3:0] Src,
  output [3:0] Dest,
  output [1:0] Sel_Add,
  output [3:0] ALU_Op,
  output Cf,
  output Zsf,
  output Stc,
  output Cmc,
  output Xchg,
  output Last,
  output [7:0] Cycle,
  output SysRST,
  output SysINT,
  output Inhibit_Inc,
  output trig,
  output stored
);

  wire condition, d_ff_1_q, disable_int, enable_q, hc163_1_tc, intoff, inton, nor_1_out, not_1_out, or_1_out,
       t0, t1, t2, trigger_q;
  wire [30:21] rom_1_data;

  not not_1 (not_1_out, CLK);
  D_Flip_Flop d_ff_1 (.D(1'b0), .clk(not_1_out), .Q(d_ff_1_q), .preset(Reset));  // open: Qn, reset
  D_Flip_Flop trigger (.D(irq), .clk(t0), .Q(trigger_q));  // open: Qn, preset, reset
  D_Flip_Flop enable (.D(1'b0), .clk(disable_int), .Q(enable_q), .preset(inton), .reset(intoff));  // open: Qn
  nor nor_1 (nor_1_out, d_ff_1_q, Last);
  and and_1 (trig, trigger_q, enable_q);
  D_Flip_Flop store (.D(trig), .clk(t1), .Q(stored));  // open: Qn, preset, reset
  hc163 hc163_1 (
    .CET(1'b1), .CEP(1'b1), .PE(1'b1), .MAR(nor_1_out), .Clock(not_1_out), .Q0(Cycle[0]), .Q1(Cycle[1]),
    .Q2(Cycle[2]), .Q3(Cycle[3]), .TC(hc163_1_tc));  // open: D0, D1, D2, D3
  hc163 hc163_2 (
    .CET(hc163_1_tc), .CEP(1'b1), .PE(1'b1), .MAR(nor_1_out), .Clock(not_1_out), .Q0(Cycle[4]),
    .Q1(Cycle[5]), .Q2(Cycle[6]), .Q3(Cycle[7]));  // open: D0, D1, D2, D3, TC
  Conditional conditional_1 (
    .ZeroF(VZero), .CarryF(VCarry), .SignF(VSign), .Instruction(Instruction), .Condition(condition));
  and and_2 (disable_int, Last, stored);
  or or_1 (or_1_out, t1, t2);
  D_Flip_Flop d_ff_2 (.D(1'b0), .clk(t1), .Q(SysRST), .preset(d_ff_1_q));  // open: Qn, reset
  and and_3 (SysINT, t0, trig);
  and and_4 (Inhibit_Inc, or_1_out, stored);
  Comparator comparator_1 (.a({8{1'b0}}), .b(Cycle), .eq(t0));  // open: gt, lt
  Comparator comparator_2 (.a(8'h1), .b(Cycle), .eq(t1));  // open: gt, lt
  Comparator comparator_3 (.a(8'h2), .b(Cycle), .eq(t2));  // open: gt, lt
  ROM #(.addrWidth(14), .dataWidth(32)) rom_1 (
    .addr({Instruction, condition, Cycle[4:0]}),
    .data({Last, rom_1_data, Xchg, Cmc, Stc, intoff, inton, Zsf, Cf, ALU_Op, Sel_Add, Dest, Src}));

  // Notes on the sheet:
  //   contents of rom_1 (hex, n*v repeats v):
  //   3df6 2199 80002588 4*0 3f76 24*0 3df6 2199 80002588 4*0 3f76 24*0 3df6 2199 2588 3d16 2199 2588 3d06
  //   2199 80002588 23*0 3df6 2199 2588 3d16 2199 2588 3d06 2199 80002588 23*0 3df6 3dd1 3dc0 3f67 2199
  //   80002588 26*0 3df6 3dd1 3dc0 3f67 2199 80002588 26*0 3df6 2111 2500 2199 80002588 27*0 3df6 2111
  //   2500 2199 80002588 27*0 3df6 a000 2199 80002588 28*0 3df6 a000 2199 80002588 28*0 3df6 a800 2199
  //   80002588 28*0 3df6 a800 2199 80002588 28*0 3df6 2199 2588 3d06 2199 80002588 26*0 3df6 2199 2588
  //   3d06 2199 80002588 26*0 3df6 4177 2577 2199 80002588 27*0 3df6 4177 2577 2199 80002588 27*0 3df6
  //   2199 80002588 29*0 3df6 2199 80002588 29*0 3df6 3dc7 3d75 4151 3d74 4540 3d7c 2199 80002588 23*0
  //   3df6 3dc7 3d75 4151 3d74 4540 3d7c 2199 80002588 23*0 3df6 3dd1 3dc0 3f76 2199 80002588 26*0 3df6
  //   3dd1 3dc0 3f76 2199 80002588 26*0 3df6 2911 2d00 2199 80002588 27*0 3df6 2911 2d00 2199 80002588
  //   27*0 3df6 a011 2199 80002588 28*0 3df6 a011 2199 80002588 28*0 3df6 a811 2199 80002588 28*0 3df6
  //   a811 2199 80002588 28*0 3df6 2199 2588 3d16 2199 80002588 26*0 3df6 2199 2588 3d16 2199 80002588
  //   26*0 3df6 7577 2199 80002588 28*0 3df6 7577 2199 80002588 28*0 3df6 2199 80002588 29*0 3df6 2199
  //   80002588 29*0 3df6 2199 2588 3d36 2199 2588 3d26 2199 80002588 23*0 3df6 2199 2588 3d36 2199 2588
  //   3d26 2199 80002588 23*0 3df6 3dd3 3dc2 3f67 2199 80002588 26*0 3df6 3dd3 3dc2 3f67 2199 80002588
  //   26*0 3df6 2133 2522 2199 80002588 27*0 3df6 2133 2522 2199 80002588 27*0 3df6 a022 2199 80002588
  //   28*0 3df6 a022 2199 80002588 28*0 3df6 a822 2199 80002588 28*0 3df6 a822 2199 80002588 28*0 3df6
  //   2199 2588 3d26 2199 80002588 26*0 3df6 2199 2588 3d26 2199 80002588 26*0 3df6 4577 2199 80002588
  //   28*0 3df6 4577 2199 80002588 28*0 3df6 2199 80002588 29*0 3df6 2199 80002588 29*0 3df6 3dc7 3d75
  //   4153 3d74 4542 3d7c 2199 80002588 23*0 3df6 3dc7 3d75 4153 3d74 4542 3d7c 2199 80002588 23*0 3df6
  //   3dd3 3dc2 3f76 2199 80002588 26*0 3df6 3dd3 3dc2 3f76 2199 80002588 26*0 3df6 2933 2d22 2199
  //   80002588 27*0 3df6 2933 2d22 2199 80002588 27*0 3df6 a033 2199 80002588 28*0 3df6 a033 2199 80002588
  //   28*0 3df6 a833 2199 80002588 28*0 3df6 a833 2199 80002588 28*0 3df6 2199 2588 3d36 2199 80002588
  //   26*0 3df6 2199 2588 3d36 2199 80002588 26*0 3df6 7177 2199 80002588 28*0 3df6 7177 2199 80002588
  //   28*0 3df6 2199 80002588 29*0 3df6 2199 80002588 29*0 3df6 2199 2588 3d56 2199 2588 3d46 2199
  //   80002588 23*0 3df6 2199 2588 3d56 2199 2588 3d46 2199 80002588 23*0 3df6 2199 2588 3dd6 2199 2588
  //   3dc6 3f65 21dd 25cc 3f64 2199 80002588 19*0 3df6 2199 2588 3dd6 2199 2588 3dc6 3f65 21dd 25cc 3f64
  //   2199 80002588 19*0 3df6 2155 2544 2199 80002588 27*0 3df6 2155 2544 2199 80002588 27*0 3df6 a044
  //   2199 80002588 28*0 3df6 a044 2199 80002588 28*0 3df6 a844 2199 80002588 28*0 3df6 a844 2199 80002588
  //   28*0 3df6 2199 2588 3d46 2199 80002588 26*0 3df6 2199 2588 3d46 2199 80002588 26*0 3df6 2199
  //   80002588 29*0 3df6 2199 80002588 29*0 3df6 2199 80002588 29*0 3df6 2199 80002588 29*0 3df6 3dc7 3d75
  //   4155 3d74 4544 3d7c 2199 80002588 23*0 3df6 3dc7 3d75 4155 3d74 4544 3d7c 2199 80002588 23*0 3df6
  //   2199 2588 3dd6 2199 2588 3dc6 3f56 21dd 25cc 3f46 2199 80002588 19*0 3df6 2199 2588 3dd6 2199 2588
  //   3dc6 3f56 21dd 25cc 3f46 2199 80002588 19*0 3df6 2955 2d44 2199 80002588 27*0 3df6 2955 2d44 2199
  //   80002588 27*0 3df6 a055 2199 80002588 28*0 3df6 a055 2199 80002588 28*0 3df6 a855 2199 80002588 28*0
  //   3df6 a855 2199 80002588 28*0 3df6 2199 2588 3d56 2199 80002588 26*0 3df6 2199 2588 3d56 2199
  //   80002588 26*0 3df6 39c7 29cc 157c 2199 80002588 26*0 3df6 39c7 29cc 157c 2199 80002588 26*0 3df6
  //   2199 80002588 29*0 3df6 2199 80002588 29*0 3df6 2199 2588 3db6 2199 2588 3da6 2199 80002588 23*0
  //   3df6 2199 2588 3db6 2199 2588 3da6 2199 80002588 23*0 3df6 2199 2588 3dd6 2199 2588 3dc6 3f67 2199
  //   80002588 22*0 3df6 2199 2588 3dd6 2199 2588 3dc6 3f67 2199 80002588 22*0 3df6 21bb 25aa 2199
  //   80002588 27*0 3df6 21bb 25aa 2199 80002588 27*0 3df6 a0c6 3c6c 2199 80002588 27*0 3df6 a0c6 3c6c
  //   2199 80002588 27*0 3df6 a8c6 3c6c 2199 80002588 27*0 3df6 a8c6 3c6c 2199 80002588 27*0 3df6 2199
  //   2588 3dc6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
endmodule

module Conditional (
  input  ZeroF,
  input  CarryF,
  input  SignF,
  input  [7:0] Instruction,
  output Condition
);

  wire decoder_1_out0, decoder_1_out1, decoder_1_out2, decoder_1_out3, nor_1_out, nor_2_out, nor_3_out,
       nor_4_out, not_1_out, not_2_out, not_3_out, not_4_out, xor_1_out, xor_2_out, xor_3_out, xor_4_out;

  Decoder #(.enable("false"), .select(2)) decoder_1 (
    .out0(decoder_1_out0), .out1(decoder_1_out1), .out2(decoder_1_out2), .out3(decoder_1_out3),
    .sel(Instruction[5:4]));
  not not_1 (not_1_out, decoder_1_out0);
  not not_2 (not_2_out, decoder_1_out1);
  not not_3 (not_3_out, decoder_1_out2);
  not not_4 (not_4_out, decoder_1_out3);
  xor xor_1 (xor_1_out, Instruction[3], ZeroF);
  xor xor_2 (xor_2_out, Instruction[3], CarryF);
  xor xor_3 (xor_3_out, Instruction[3], 1'b0);
  xor xor_4 (xor_4_out, Instruction[3], SignF);
  nor nor_1 (nor_1_out, not_1_out, xor_1_out);
  nor nor_2 (nor_2_out, not_2_out, xor_2_out);
  nor nor_3 (nor_3_out, not_3_out, xor_3_out);
  nor nor_4 (nor_4_out, not_4_out, xor_4_out);
  or or_1 (Condition, nor_1_out, nor_2_out, nor_3_out, nor_4_out);
endmodule

module hc163 (
  input  D0,
  input  D1,
  input  D2,
  input  D3,
  input  CET,
  input  CEP,
  input  PE,
  input  MAR,
  input  Clock,
  output Q0,
  output Q1,
  output Q2,
  output Q3,
  output TC
);

  wire and_1_out, and_2_out, and_3_out, and_4_out, and_5_out, and_6_out, and_7_out, and_8_out, and_9_out,
       d_ff_1_q, d_ff_1_qn, d_ff_2_q, d_ff_2_qn, d_ff_3_q, d_ff_3_qn, d_ff_4_q, d_ff_4_qn, nand_1_out,
       nand_2_out, nor_1_out, nor_2_out, nor_3_out, nor_4_out, nor_5_out, nor_6_out, not_1_out, not_2_out,
       or_1_out, or_2_out, or_3_out, or_4_out, or_5_out, xnor_1_out, xnor_2_out, xnor_3_out;

  nand nand_1 (nand_1_out, CET, CEP);
  nor nor_1 (nor_1_out, PE, not_1_out);
  not not_1 (not_1_out, MAR);
  nor nor_2 (nor_2_out, nor_1_out, not_1_out);
  and and_1 (and_1_out, D0, nor_1_out);
  not not_2 (not_2_out, nand_1_out);
  xnor xnor_1 (xnor_1_out, not_2_out, d_ff_1_qn);
  and and_2 (and_2_out, xnor_1_out, nor_2_out);
  or or_1 (or_1_out, and_1_out, and_2_out);
  D_Flip_Flop d_ff_1 (.D(or_1_out), .clk(Clock), .Q(d_ff_1_q), .Qn(d_ff_1_qn));  // open: preset, reset
  nor nor_3 (nor_3_out, nand_1_out, d_ff_1_qn);
  and and_3 (and_3_out, D1, nor_1_out);
  or or_2 (or_2_out, and_3_out, and_4_out);
  not not_3 (Q0, d_ff_1_qn);
  xnor xnor_2 (xnor_2_out, nor_3_out, d_ff_2_qn);
  and and_4 (and_4_out, xnor_2_out, nor_2_out);
  D_Flip_Flop d_ff_2 (.D(or_2_out), .clk(Clock), .Q(d_ff_2_q), .Qn(d_ff_2_qn));  // open: preset, reset
  nor nor_4 (nor_4_out, nand_1_out, d_ff_1_qn, d_ff_2_qn);
  and and_5 (and_5_out, D2, nor_1_out);
  or or_3 (or_3_out, and_5_out, and_6_out);
  not not_4 (Q1, d_ff_2_qn);
  xnor xnor_3 (xnor_3_out, nor_4_out, d_ff_3_qn);
  and and_6 (and_6_out, xnor_3_out, nor_2_out);
  D_Flip_Flop d_ff_3 (.D(or_3_out), .clk(Clock), .Q(d_ff_3_q), .Qn(d_ff_3_qn));  // open: preset, reset
  and and_7 (and_7_out, D3, nor_1_out);
  not not_5 (Q2, d_ff_3_qn);
  nor nor_5 (nor_5_out, nand_1_out, d_ff_1_qn, d_ff_2_qn, d_ff_3_qn);
  and and_8 (and_8_out, nor_5_out, d_ff_4_qn);
  nor nor_6 (nor_6_out, nor_5_out, d_ff_4_qn);
  or or_4 (or_4_out, and_8_out, nor_6_out);
  and and_9 (and_9_out, nor_2_out, or_4_out);
  or or_5 (or_5_out, and_7_out, and_9_out);
  D_Flip_Flop d_ff_4 (.D(or_5_out), .clk(Clock), .Q(d_ff_4_q), .Qn(d_ff_4_qn));  // open: preset, reset
  nand nand_2 (nand_2_out, d_ff_4_q, d_ff_3_q, d_ff_2_q, d_ff_1_q, CET);
  not not_6 (Q3, d_ff_4_qn);
  not not_7 (TC, nand_2_out);

  // Notes on the sheet:
  //   Drawn from the Nexperia datasheet at: https;//assets.nexperia.com/documents/data-sheet74HC_HCT163_Q100.pdf
endmodule

module Rotate (
  input  [7:0] Input_ALU,
  input  [7:0] Input_acc,
  input  Stored_carry,
  input  Live_carry,
  input  Rar,
  input  Rrc,
  input  flip_c,
  output [7:0] Result,
  output Carry_out
);

  wire multiplexer_3_out, not_1_out, or_1_out;
  wire [7:7] multiplexer_1_out;

  Multiplexer multiplexer_1 (.in0(Stored_carry), .in1(Input_acc[0]), .out(multiplexer_1_out[7]), .sel(Rrc));
  or or_1 (or_1_out, Rar, Rrc);
  Multiplexer #(.width(8)) multiplexer_2 (
    .in0(Input_ALU), .in1({multiplexer_1_out[7], Input_acc[7:1]}), .out(Result), .sel(or_1_out));
  Multiplexer multiplexer_3 (.in0(Live_carry), .in1(Input_acc[0]), .out(multiplexer_3_out), .sel(or_1_out));
  not not_1 (not_1_out, multiplexer_3_out);
  Multiplexer multiplexer_4 (.in0(multiplexer_3_out), .in1(not_1_out), .out(Carry_out), .sel(flip_c));
endmodule

module hc181 (
  input  [3:0] S,
  input  [3:0] A,
  input  [3:0] B,
  input  M,
  input  Cin,
  output [3:0] F,
  output G,
  output C4,
  output P,
  output AeqB
);

  wire and_1_out, and_2_out, and_3_out, and_4_out, and_5_out, and_6_out, and_7_out, and_8_out, and_9_out,
       and_10_out, and_11_out, and_12_out, and_13_out, and_14_out, and_15_out, and_16_out, and_17_out,
       and_18_out, and_19_out, and_20_out, and_21_out, and_22_out, and_23_out, and_24_out, and_25_out,
       and_26_out, and_27_out, and_28_out, and_29_out, and_30_out, and_31_out, and_32_out, and_33_out,
       and_34_out, and_35_out, and_36_out, and_37_out, nand_1_out, nand_3_out, nor_1_out, nor_2_out,
       nor_3_out, nor_4_out, nor_5_out, nor_6_out, nor_7_out, nor_8_out, nor_10_out, nor_11_out, nor_12_out,
       not_1_out, not_2_out, not_3_out, not_4_out, not_5_out, not_6_out, not_7_out, not_8_out, not_9_out;

  not not_1 (not_1_out, B[3]);
  not not_2 (not_2_out, B[2]);
  not not_3 (not_3_out, B[1]);
  not not_4 (not_4_out, B[0]);
  and and_1 (and_1_out, S[3], B[3], A[3]);
  and and_2 (and_2_out, A[3], S[2], not_1_out);
  and and_3 (and_3_out, not_1_out, S[1]);
  and and_4 (and_4_out, S[0], B[3]);
  and and_5 (and_5_out, A[3], A[3]);
  and and_6 (and_6_out, S[3], B[2], A[2]);
  and and_7 (and_7_out, A[2], S[2], not_2_out);
  and and_8 (and_8_out, not_2_out, S[1]);
  and and_9 (and_9_out, S[0], B[2]);
  and and_10 (and_10_out, A[2], A[2]);
  and and_11 (and_11_out, S[3], B[1], A[1]);
  and and_12 (and_12_out, A[1], S[2], not_3_out);
  and and_13 (and_13_out, not_3_out, S[1]);
  and and_14 (and_14_out, S[0], B[1]);
  and and_15 (and_15_out, A[1], A[1]);
  and and_16 (and_16_out, S[3], B[0], A[0]);
  and and_17 (and_17_out, A[0], S[2], not_4_out);
  and and_18 (and_18_out, not_4_out, S[1]);
  and and_19 (and_19_out, S[0], B[0]);
  and and_20 (and_20_out, A[0], A[0]);
  nor nor_1 (nor_1_out, and_1_out, and_2_out);
  nor nor_2 (nor_2_out, and_3_out, and_4_out, and_5_out);
  nor nor_3 (nor_3_out, and_6_out, and_7_out);
  nor nor_4 (nor_4_out, and_8_out, and_9_out, and_10_out);
  nor nor_5 (nor_5_out, and_11_out, and_12_out);
  nor nor_6 (nor_6_out, and_13_out, and_14_out, and_15_out);
  nor nor_7 (nor_7_out, and_16_out, and_17_out);
  nor nor_8 (nor_8_out, and_18_out, and_19_out, and_20_out);
  not not_5 (not_5_out, M);
  and and_21 (and_21_out, nor_2_out, nor_2_out);
  and and_22 (and_22_out, nor_1_out, nor_4_out);
  and and_23 (and_23_out, nor_1_out, nor_3_out, nor_6_out);
  and and_24 (and_24_out, nor_1_out, nor_3_out, nor_5_out, nor_8_out);
  nand nand_1 (nand_1_out, nor_1_out, nor_3_out, nor_5_out, nor_7_out, Cin);
  nand nand_2 (P, nor_1_out, nor_3_out, nor_5_out, nor_7_out);
  not not_6 (not_6_out, nor_2_out);
  and and_25 (and_25_out, nor_3_out, nor_5_out, nor_7_out, Cin, not_5_out);
  and and_26 (and_26_out, nor_3_out, nor_5_out, nor_8_out, not_5_out);
  and and_27 (and_27_out, nor_3_out, nor_6_out, not_5_out);
  and and_28 (and_28_out, nor_4_out, not_5_out);
  not not_7 (not_7_out, nor_4_out);
  and and_29 (and_29_out, nor_5_out, nor_7_out, Cin, not_5_out);
  and and_30 (and_30_out, nor_5_out, nor_8_out, not_5_out);
  and and_31 (and_31_out, nor_6_out, not_5_out);
  not not_8 (not_8_out, nor_6_out);
  and and_32 (and_32_out, nor_7_out, Cin, not_5_out);
  and and_33 (and_33_out, nor_8_out, not_5_out);
  not not_9 (not_9_out, nor_8_out);
  nand nand_3 (nand_3_out, not_5_out, Cin);
  nor nor_9 (G, and_21_out, and_22_out, and_23_out, and_24_out);
  and and_34 (and_34_out, nor_1_out, not_6_out);
  xor xor_1 (F[3], and_34_out, nor_10_out);
  nor nor_10 (nor_10_out, and_25_out, and_26_out, and_27_out, and_28_out);
  and and_35 (and_35_out, nor_3_out, not_7_out);
  xor xor_2 (F[2], and_35_out, nor_11_out);
  nor nor_11 (nor_11_out, and_29_out, and_30_out, and_31_out);
  and and_36 (and_36_out, nor_5_out, not_8_out);
  xor xor_3 (F[1], and_36_out, nor_12_out);
  nor nor_12 (nor_12_out, and_32_out, and_33_out);
  and and_37 (and_37_out, nor_7_out, not_9_out);
  xor xor_4 (F[0], and_37_out, nand_3_out);
  or or_1 (C4, ~G, ~nand_1_out);  // OR_Gate
  and and_38 (AeqB, F[3], F[2], F[1], F[0]);
endmodule

module ALU_internal (
  input  [3:0] Sel,
  input  Cext,
  input  Cint,
  input  Int,
  output [3:0] Command,
  output m,
  output c,
  output b2a,
  output rar,
  output rrc,
  output c_flipped
);

  wire and_1_out, and_2_out, and_3_out, and_4_out, and_5_out, and_6_out, and_7_out, and_8_out, and_9_out,
       and_10_out, and_11_out, and_12_out, and_13_out, and_14_out, and_15_out, and_16_out, and_17_out,
       and_18_out, and_19_out, and_20_out, and_21_out, and_24_out, and_25_out, multiplexer_1_out,
       multiplexer_2_out, not_1_out, not_2_out, not_3_out, not_4_out, not_5_out, or_5_out, or_6_out;
  wire [3:0] or_4_out;

  not not_1 (not_1_out, Cext);
  Multiplexer multiplexer_1 (.in0(not_1_out), .in1(Cext), .out(multiplexer_1_out), .sel(c_flipped));
  Multiplexer multiplexer_2 (.in0(multiplexer_1_out), .in1(Cint), .out(multiplexer_2_out), .sel(Sel[3]));
  not not_2 (not_2_out, Sel[3]);
  not not_3 (not_3_out, Sel[2]);
  not not_4 (not_4_out, Sel[1]);
  not not_5 (not_5_out, Sel[0]);
  and and_1 (and_1_out, not_2_out, not_3_out, not_4_out);
  and and_2 (and_2_out, not_2_out, Sel[2], not_5_out);
  and and_3 (and_3_out, Sel[3], not_3_out, Sel[1]);
  and and_4 (and_4_out, not_2_out, Sel[1]);
  and and_5 (and_5_out, not_3_out, Sel[1]);
  and and_6 (and_6_out, not_2_out, Sel[2], Sel[0]);
  and and_7 (and_7_out, not_3_out, Sel[1]);
  and and_8 (and_8_out, Sel[1], not_5_out);
  and and_9 (and_9_out, not_2_out, Sel[2]);
  and and_10 (and_10_out, not_2_out, not_3_out, not_4_out);
  and and_11 (and_11_out, not_2_out, not_4_out, not_5_out);
  and and_12 (and_12_out, Sel[3], not_3_out, Sel[1]);
  and and_13 (and_13_out, Sel[3], Sel[1], not_5_out);
  and and_14 (and_14_out, not_2_out, Sel[2], not_4_out);
  and and_15 (and_15_out, not_2_out, Sel[2], not_5_out);
  and and_16 (and_16_out, not_2_out, not_4_out);
  and and_17 (and_17_out, Sel[3], not_3_out, Sel[1]);
  and and_18 (and_18_out, Sel[3], Sel[1], Sel[0]);
  and and_19 (and_19_out, Sel[3], not_3_out);
  and and_20 (and_20_out, Sel[3], Sel[1], Sel[0]);
  and and_21 (and_21_out, not_3_out, Sel[0]);
  and and_22 (rar, Sel[3], Sel[2], not_4_out, not_5_out);
  and and_23 (rrc, Sel[3], Sel[2], not_4_out, Sel[0]);
  and and_24 (and_24_out, not_2_out, Sel[1], Sel[0]);
  and and_25 (and_25_out, not_2_out, not_3_out, Sel[1]);
  or or_1 (or_4_out[3], and_1_out, and_2_out, and_3_out);
  or or_2 (or_4_out[2], and_4_out, and_5_out, and_6_out);
  or or_3 (or_4_out[1], and_7_out, and_8_out, and_9_out);
  or or_4 (or_4_out[0], and_10_out, and_11_out, and_12_out, and_13_out);
  or or_5 (or_5_out, and_14_out, and_15_out);
  or or_6 (or_6_out, and_16_out, and_17_out, and_18_out);
  Multiplexer multiplexer_3 (.in0(or_6_out), .in1(multiplexer_2_out), .out(c), .sel(and_21_out));
  or or_7 (b2a, and_19_out, and_20_out);
  or or_8 (c_flipped, and_24_out, and_25_out);
  assign Command = or_4_out | {4{Int}};  // OR_Gate or_9, 4 bits wide
  or or_10 (m, or_5_out, Int);
endmodule

module Fake8080 (
  input  [15:0] in_1,
  input  run
);

  wire Clk, keyboard_1_avail, nand_1_out, not_1_out, not_2_out, processor_1_last, processor_1_rnw, Ram_En,
       RST_out, Ser_In, Ser_Out, step_out;
  wire [3:0] processor_1_debug_a, processor_1_debug_a_2, processor_1_debug_bc, processor_1_debug_bc_2,
       processor_1_debug_bc_3, processor_1_debug_bc_4, processor_1_debug_de, processor_1_debug_de_2,
       processor_1_debug_de_3, processor_1_debug_de_4, processor_1_debug_hl, processor_1_debug_hl_2,
       processor_1_debug_hl_3, processor_1_debug_hl_4, processor_1_debug_sp, processor_1_debug_sp_2,
       processor_1_debug_sp_3, processor_1_debug_sp_4;
  wire [6:0] keyboard_1_data;
  wire [7:0] Din;
  wire [15:0] Address_Bus;

  TTY #(.cols(40), .rows(16)) tty_1 (.data(Din[6:0]), .clk(Clk), .we(Ser_Out));  // open: clr
  Clock clock_1 (.out(Clk));
  Button RST (.out(RST_out));
  Button step (.out(step_out));
  Keyboard #(.buflen(64)) keyboard_1 (
    .clk(Clk), .re(Ser_In), .avail(keyboard_1_avail), .data(keyboard_1_data));  // open: clr
  Hex_Digit_Display hex_digit_display_1 (.value(processor_1_debug_a_2));  // open: dp
  Hex_Digit_Display hex_digit_display_2 (.value(processor_1_debug_a));  // open: dp
  assign Din = Ser_In ? {1'b0, keyboard_1_data} : 8'bz;  // Controlled_Buffer controlled_buffer_1
  Hex_Digit_Display hex_digit_display_3 (.value(processor_1_debug_bc_4));  // open: dp
  Processor processor_1 (
    .Clk(Clk), .DataIn(Din), .Rst(RST_out), .halt(in_1), .run(run), .single(step_out),
    .debug_a({processor_1_debug_a_2, processor_1_debug_a}),
    .debug_bc({processor_1_debug_bc_4, processor_1_debug_bc_3, processor_1_debug_bc_2, processor_1_debug_bc}),
    .debug_de({processor_1_debug_de_4, processor_1_debug_de_3, processor_1_debug_de_2, processor_1_debug_de}),
    .debug_hl({processor_1_debug_hl_4, processor_1_debug_hl_3, processor_1_debug_hl_2, processor_1_debug_hl}),
    .debug_sp({processor_1_debug_sp_4, processor_1_debug_sp_3, processor_1_debug_sp_2, processor_1_debug_sp}),
    .Address(Address_Bus), .DataOut(Din), .RnW(processor_1_rnw), .last(processor_1_last));  // open: Interrupt
  LED led_1 (.in(processor_1_last));
  Hex_Digit_Display hex_digit_display_4 (.value(processor_1_debug_bc_3));  // open: dp
  Hex_Digit_Display hex_digit_display_5 (.value(processor_1_debug_bc_2));  // open: dp
  Hex_Digit_Display hex_digit_display_6 (.value(processor_1_debug_bc));  // open: dp
  nand nand_1 (nand_1_out, processor_1_rnw, Ram_En);
  Hex_Digit_Display hex_digit_display_7 (.value(processor_1_debug_de_4));  // open: dp
  Hex_Digit_Display hex_digit_display_8 (.value(processor_1_debug_de_3));  // open: dp
  RAM #(.addrWidth(16), .asyncread("true"), .databus("bidir")) ram_1 (
    .addr(Address_Bus), .we(nand_1_out), .oe(not_1_out), .clk(Clk), .data(Din));
  not not_1 (not_1_out, nand_1_out);
  Hex_Digit_Display hex_digit_display_9 (.value(processor_1_debug_de));  // open: dp
  Hex_Digit_Display hex_digit_display_10 (.value(processor_1_debug_de_2));  // open: dp
  Decoder #(.select(4)) decoder_1 (
    .out0(Ser_In), .out1(Ser_Out), .sel(Address_Bus[11:8]), .en(not_2_out));  // open: out2, out3, out4, out5, out6, out7, out8, out9, out10, out11, out12, out13, out14, out15
  nand nand_2 (Ram_En, Address_Bus[12], Address_Bus[13], Address_Bus[14], Address_Bus[15]);
  Hex_Digit_Display hex_digit_display_11 (.value(processor_1_debug_hl_4));  // open: dp
  not not_2 (not_2_out, Ram_En);
  Hex_Digit_Display hex_digit_display_12 (.value(processor_1_debug_hl_3));  // open: dp
  Hex_Digit_Display hex_digit_display_13 (.value(processor_1_debug_hl_2));  // open: dp
  Hex_Digit_Display hex_digit_display_14 (.value(processor_1_debug_hl));  // open: dp
  // Probe on Din
  Hex_Digit_Display hex_digit_display_15 (.value(processor_1_debug_sp_4));  // open: dp
  Hex_Digit_Display hex_digit_display_16 (.value(processor_1_debug_sp_3));  // open: dp
  Hex_Digit_Display hex_digit_display_17 (.value(processor_1_debug_sp_2));  // open: dp
  Hex_Digit_Display hex_digit_display_18 (.value(processor_1_debug_sp));  // open: dp

  // Other names for the same wires on the sheet: Dout[7:0] = Din

  // Notes on the sheet:
  //   A (7)
  //   B (0)
  //   C (1)
  //   D (2)
  //   E (3)
  //   H (4)
  //   L (5)
  //   SP
endmodule

module xchg (
  input  flip,
  input  [3:0] dest,
  output [3:0] res
);

  wire and_1_out, and_2_out, and_3_out, and_4_out, and_5_out, and_6_out, not_1_out, not_2_out;

  not not_1 (not_1_out, flip);
  not not_2 (not_2_out, dest[3]);
  and and_1 (and_1_out, not_1_out, dest[2]);
  and and_2 (and_2_out, dest[3], dest[2]);
  and and_3 (and_3_out, flip, not_2_out, dest[1]);
  and and_4 (and_4_out, not_1_out, dest[1]);
  and and_5 (and_5_out, dest[3], dest[1]);
  and and_6 (and_6_out, flip, not_2_out, dest[2]);
  or or_1 (res[2], and_1_out, and_2_out, and_3_out);
  or or_2 (res[1], and_4_out, and_5_out, and_6_out);

  assign {res[3], res[0]} = {dest[3], dest[0]};
endmodule
